// Logisim project e2449049.circ as structural Verilog: 2 circuits, main circuit main
module main (
  input  A1,
  input  A0,
  input  B1,
  input  B0,
  input  _02,
  input  O1,
  input  O0,
  input  O3,
  output P,
  output C,
  output L6,
  output L5,
  output L4,
  output L3,
  output L2,
  output L1,
  output L0,
  output Z,
  output E,
  output G,
  output L,
  output S,
  output L9,
  output L8,
  output L7
);

  wire and_1_out, and_2_out, and_3_out, and_4_out, and_5_out, and_6_out, and_7_out, and_8_out, and_9_out,
       and_10_out, and_11_out, and_12_out, and_13_out, and_14_out, and_15_out, and_16_out, and_17_out,
       and_18_out, and_19_out, and_20_out, and_21_out, and_22_out, and_23_out, and_24_out, and_25_out,
       and_26_out, and_27_out, and_28_out, and_29_out, and_30_out, and_31_out, and_32_out, and_33_out,
       and_34_out, and_35_out, and_36_out, and_37_out, and_38_out, and_39_out, and_40_out, and_41_out,
       and_42_out, and_43_out, and_44_out, and_45_out, and_46_out, and_47_out, and_48_out, and_49_out,
       and_50_out, and_51_out, and_52_out, and_53_out, and_54_out, and_55_out, and_56_out, and_57_out,
       and_58_out, and_59_out, and_60_out, and_61_out, and_62_out, and_63_out, and_64_out, and_65_out,
       and_66_out, and_67_out, and_68_out, and_69_out, and_70_out, controlled_buffer_1_out,
       controlled_buffer_2_out, controlled_buffer_3_out, controlled_buffer_5_out, controlled_buffer_6_out,
       controlled_buffer_7_out, controlled_buffer_8_out, controlled_buffer_9_out, controlled_buffer_10_out,
       controlled_buffer_11_out, controlled_buffer_12_out, controlled_buffer_13_out,
       controlled_buffer_14_out, controlled_buffer_15_out, controlled_buffer_16_out,
       controlled_buffer_17_out, controlled_buffer_18_out, controlled_buffer_19_out,
       controlled_buffer_21_out, controlled_buffer_22_out, controlled_buffer_23_out,
       controlled_buffer_24_out, controlled_inverter_1_out, n3_to_8_decoder_74138_1_p7,
       n3_to_8_decoder_74138_1_p8, n3_to_8_decoder_74138_1_p9, n3_to_8_decoder_74138_1_p10,
       n3_to_8_decoder_74138_2_p7, n3_to_8_decoder_74138_2_p8, n3_to_8_decoder_74138_2_p9,
       n3_to_8_decoder_74138_2_p10, n3_to_8_decoder_74138_2_p11, n3_to_8_decoder_74138_2_p12,
       n3_to_8_decoder_74138_3_p3, n3_to_8_decoder_74138_3_p5, n3_to_8_decoder_74138_3_p7,
       n3_to_8_decoder_74138_3_p8, n3_to_8_decoder_74138_3_p9, n3_to_8_decoder_74138_3_p10,
       n3_to_8_decoder_74138_3_p11, n4_to_1_mux_x2_74153_1_p11, n4_to_1_mux_x2_74153_1_p12,
       n4_to_1_mux_x2_74153_2_p7, n4_to_1_mux_x2_74153_2_p11, n4_to_1_mux_x2_74153_2_p12, not_1_out,
       not_2_out, not_3_out, not_4_out, not_5_out, not_6_out, not_7_out, not_8_out, not_9_out, not_10_out,
       not_11_out, not_12_out, not_13_out, not_14_out, not_15_out, not_16_out, not_17_out, not_18_out,
       not_19_out, not_21_out, not_22_out, not_23_out, not_24_out, not_25_out, not_26_out, not_27_out,
       not_28_out, not_29_out, not_30_out, not_31_out, not_32_out, not_33_out, not_34_out, not_35_out,
       not_36_out, not_37_out, not_38_out, not_39_out, not_40_out, not_41_out, not_42_out, not_43_out,
       not_44_out, not_45_out, not_46_out, or_1_out, or_2_out, or_3_out, or_4_out, or_5_out, or_6_out,
       or_7_out, or_8_out, or_9_out, or_10_out, or_11_out, or_12_out, or_13_out, or_14_out, or_15_out,
       or_16_out, or_17_out, or_18_out, or_19_out, or_20_out, or_21_out, or_22_out, or_24_out, or_25_out,
       or_31_out, or_32_out, or_33_out, or_34_out, or_35_out, or_36_out, or_37_out, xor_1_out, xor_2_out,
       xor_3_out, xor_4_out;

  not not_1 (not_1_out, A1);
  not not_2 (not_2_out, A0);
  not not_3 (not_3_out, B0);
  not not_4 (not_4_out, B1);
  and and_1 (and_1_out, A0, not_4_out);
  and and_2 (and_2_out, A1, not_3_out);
  and and_3 (and_3_out, A1, A0);
  and and_4 (and_4_out, A0, B1);
  and and_5 (and_5_out, A1, A0);
  and and_6 (and_6_out, not_1_out, A0);
  and and_7 (and_7_out, not_4_out, B0);
  and and_8 (and_8_out, A1, A0);
  and and_9 (and_9_out, B1, B0);
  and and_10 (and_10_out, not_1_out, not_2_out);
  and and_11 (and_11_out, not_1_out, B1);
  and and_12 (and_12_out, A1, not_2_out);
  and and_13 (and_13_out, A1, not_4_out);
  and and_14 (and_14_out, B0, A0);
  and and_15 (and_15_out, B1, A1);
  and and_16 (and_16_out, B0, not_2_out);
  and and_17 (and_17_out, A0, not_3_out);
  and and_18 (and_18_out, not_1_out, not_2_out);
  and and_19 (and_19_out, not_2_out, B1);
  and and_20 (and_20_out, not_1_out, B1);
  and and_21 (and_21_out, not_1_out, not_2_out);
  and and_22 (and_22_out, A1, not_4_out);
  and and_23 (and_23_out, not_1_out, B1);
  and and_24 (and_24_out, A1, A0);
  and and_25 (and_25_out, not_2_out, B0);
  and and_26 (and_26_out, A0, not_3_out);
  and and_27 (and_27_out, A1, B1);
  and and_28 (and_28_out, A0, B1);
  and and_29 (and_29_out, A1, B0);
  and and_30 (and_30_out, A0, B0);
  and and_31 (and_31_out, B0, B1);
  and and_32 (and_32_out, A0, A1);
  or or_1 (or_1_out, A1, B1);
  or or_2 (or_2_out, A0, B0);
  and and_33 (and_33_out, A1, not_2_out);
  and and_34 (and_34_out, B1, B0);
  and and_35 (and_35_out, A0, not_1_out);
  or or_3 (or_3_out, and_1_out, and_2_out);
  and and_36 (and_36_out, and_6_out, and_7_out);
  and and_37 (and_37_out, and_8_out, and_9_out);
  and and_38 (and_38_out, B1, and_10_out);
  and and_39 (and_39_out, not_3_out, and_11_out);
  and and_40 (and_40_out, not_4_out, and_12_out);
  and and_41 (and_41_out, not_3_out, and_13_out);
  xor xor_1 (xor_1_out, B0, A0);
  xor xor_2 (xor_2_out, B1, A1);
  not not_5 (not_5_out, xor_3_out);
  xor xor_3 (xor_3_out, A1, B1);
  xor xor_4 (xor_4_out, A0, B0);
  not not_6 (not_6_out, xor_4_out);
  and and_42 (and_42_out, A0, not_4_out);
  and and_43 (and_43_out, A1, A0);
  and and_44 (and_44_out, A1, not_4_out);
  and and_45 (and_45_out, and_18_out, B0);
  and and_46 (and_46_out, and_19_out, B0);
  and and_47 (and_47_out, and_21_out, B1);
  and and_48 (and_48_out, and_22_out, not_3_out);
  and and_49 (and_49_out, and_23_out, B0);
  and and_50 (and_50_out, and_24_out, not_4_out);
  or or_4 (or_4_out, and_25_out, and_26_out);
  and and_51 (and_51_out, and_31_out, and_32_out);
  and and_52 (and_52_out, and_4_out, B0);
  and and_53 (and_53_out, and_5_out, B0);
  and and_54 (and_54_out, A1, B1);
  or or_5 (or_5_out, and_36_out, and_37_out);
  or or_6 (or_6_out, and_38_out, and_39_out);
  or or_7 (or_7_out, and_40_out, and_41_out);
  or or_8 (or_8_out, and_16_out, and_17_out);
  and and_55 (and_55_out, not_5_out, not_6_out);
  and and_56 (and_56_out, and_42_out, not_3_out);
  and and_57 (and_57_out, and_43_out, not_3_out);
  or or_9 (or_9_out, and_45_out, and_46_out);
  or or_10 (or_10_out, and_47_out, and_48_out);
  or or_11 (or_11_out, and_49_out, and_50_out);
  or or_12 (or_12_out, and_28_out, and_29_out);
  and and_58 (and_58_out, and_33_out, and_34_out);
  and and_59 (and_59_out, and_34_out, and_35_out);
  and and_60 (and_60_out, A1, A0);
  and and_61 (and_61_out, A1, not_4_out);
  or or_13 (or_13_out, or_3_out, and_3_out);
  or or_14 (or_14_out, and_52_out, and_53_out);
  or or_15 (or_15_out, or_5_out, or_6_out);
  or or_16 (or_16_out, and_56_out, and_57_out);
  or or_17 (or_17_out, or_9_out, and_20_out);
  or or_18 (or_18_out, or_10_out, or_11_out);
  and and_62 (and_62_out, not_3_out, and_60_out);
  or or_19 (or_19_out, or_14_out, and_54_out);
  or or_20 (or_20_out, or_15_out, or_7_out);
  // _3_to_8_decoder__74138 #(.Facing("east")) 3_to_8_decoder_74138_1: pin names not known; wires that end beside it: or_2_out, or_1_out, 1'b0, 1'b1, 1'b0, 1'b0, n3_to_8_decoder_74138_1_p7, n3_to_8_decoder_74138_1_p8, n3_to_8_decoder_74138_1_p9, n3_to_8_decoder_74138_1_p10
  or or_21 (or_21_out, and_59_out, and_62_out);
  assign controlled_buffer_1_out = and_63_out ? and_55_out : 1'bz;  // Controlled_Buffer controlled_buffer_1
  or or_22 (or_22_out, or_16_out, and_44_out);
  and and_63 (and_63_out, not_11_out, and_64_out);
  assign controlled_buffer_2_out = and_63_out ? or_22_out : 1'bz;  // Controlled_Buffer controlled_buffer_2
  // _3_to_8_decoder__74138 #(.Facing("east")) 3_to_8_decoder_74138_2: pin names not known; wires that end beside it: and_30_out, or_12_out, and_27_out, 1'b1, 1'b0, 1'b0, n3_to_8_decoder_74138_2_p7, n3_to_8_decoder_74138_2_p8, n3_to_8_decoder_74138_2_p9, n3_to_8_decoder_74138_2_p10, n3_to_8_decoder_74138_2_p11, n3_to_8_decoder_74138_2_p12
  not not_7 (not_7_out, n3_to_8_decoder_74138_1_p7);
  not not_8 (not_8_out, n3_to_8_decoder_74138_1_p8);
  not not_9 (not_9_out, n3_to_8_decoder_74138_1_p9);
  not not_10 (not_10_out, n3_to_8_decoder_74138_1_p10);
  not not_11 (not_11_out, O1);
  assign controlled_buffer_3_out = controlled_buffer_1_out ? 1'b0 : 1'bz;  // Controlled_Buffer controlled_buffer_3
  not not_12 (not_12_out, controlled_buffer_2_out);
  assign controlled_buffer_3_out = not_13_out ? not_12_out : 1'bz;  // Controlled_Buffer controlled_buffer_4
  not not_13 (not_13_out, controlled_buffer_1_out);
  not not_14 (not_14_out, n3_to_8_decoder_74138_2_p7);
  not not_15 (not_15_out, n3_to_8_decoder_74138_2_p8);
  not not_16 (not_16_out, n3_to_8_decoder_74138_2_p9);
  not not_17 (not_17_out, n3_to_8_decoder_74138_2_p10);
  not not_18 (not_18_out, n3_to_8_decoder_74138_2_p11);
  not not_19 (not_19_out, n3_to_8_decoder_74138_2_p12);
  and and_64 (and_64_out, _02, O0);
  assign controlled_buffer_5_out = and_66_out ? and_51_out : 1'bz;  // Controlled_Buffer controlled_buffer_5
  // _4_to_1_MUX__x2___74153 #(.Facing("east")) 4_to_1_mux_x2_74153_1: pin names not known; wires that end beside it: and_58_out, and_61_out, or_20_out, or_21_out, or_13_out, or_8_out, _02, O0, _02, O1, n4_to_1_mux_x2_74153_1_p11, n4_to_1_mux_x2_74153_1_p12
  // _4_to_1_MUX__x2___74153 #(.Facing("east")) 4_to_1_mux_x2_74153_2: pin names not known; wires that end beside it: or_18_out, and_15_out, xor_2_out, or_4_out, and_14_out, xor_1_out, n4_to_1_mux_x2_74153_2_p7, O0, n4_to_1_mux_x2_74153_2_p7, O1, n4_to_1_mux_x2_74153_2_p11, n4_to_1_mux_x2_74153_2_p12
  assign controlled_buffer_6_out = O3 ? not_7_out : 1'bz;  // Controlled_Buffer controlled_buffer_6
  assign controlled_buffer_7_out = O3 ? not_8_out : 1'bz;  // Controlled_Buffer controlled_buffer_7
  or or_23 (E, 1'b0, controlled_buffer_1_out);
  assign controlled_buffer_8_out = O3 ? not_9_out : 1'bz;  // Controlled_Buffer controlled_buffer_8
  not not_20 (n4_to_1_mux_x2_74153_2_p7, _02);
  or or_24 (or_24_out, n4_to_1_mux_x2_74153_1_p11, n4_to_1_mux_x2_74153_2_p11);
  or or_25 (or_25_out, n4_to_1_mux_x2_74153_1_p12, n4_to_1_mux_x2_74153_2_p12);
  not not_21 (not_21_out, O1);
  not not_22 (not_22_out, _02);
  and and_65 (and_65_out, not_22_out, not_21_out);
  and and_66 (and_66_out, and_65_out, O0);
  or or_26 (L9, controlled_buffer_5_out, 1'b0);
  assign controlled_buffer_9_out = O3 ? not_10_out : 1'bz;  // Controlled_Buffer controlled_buffer_9
  and and_67 (and_67_out, O0, O1);
  or or_27 (G, 1'b0, controlled_buffer_2_out);
  or or_28 (L, controlled_buffer_3_out, 1'b0);
  not not_23 (not_23_out, O0);
  and and_68 (and_68_out, _02, not_24_out);
  not not_24 (not_24_out, O1);
  assign controlled_buffer_10_out = and_69_out ? or_19_out : 1'bz;  // Controlled_Buffer controlled_buffer_10
  and and_69 (and_69_out, and_67_out, n4_to_1_mux_x2_74153_2_p7);
  assign controlled_inverter_1_out = and_70_out ? ~or_17_out : 1'bz;  // Controlled_Inverter controlled_inverter_1
  and and_70 (and_70_out, not_23_out, and_68_out);
  or or_29 (C, controlled_buffer_10_out, 1'b0);
  // _3_to_8_decoder__74138 #(.Facing("south")) 3_to_8_decoder_74138_3: pin names not known; wires that end beside it: and_67_out, or_25_out, n3_to_8_decoder_74138_3_p3, or_24_out, n3_to_8_decoder_74138_3_p5, C, n3_to_8_decoder_74138_3_p7, n3_to_8_decoder_74138_3_p8, n3_to_8_decoder_74138_3_p9, n3_to_8_decoder_74138_3_p10, n3_to_8_decoder_74138_3_p11, 1'b1, 1'b0, 1'b0
  not not_25 (not_25_out, n3_to_8_decoder_74138_3_p11);
  not not_26 (not_26_out, n3_to_8_decoder_74138_3_p10);
  not not_27 (not_27_out, n3_to_8_decoder_74138_3_p9);
  not not_28 (not_28_out, n3_to_8_decoder_74138_3_p8);
  not not_29 (not_29_out, n3_to_8_decoder_74138_3_p7);
  not not_30 (not_30_out, n3_to_8_decoder_74138_3_p5);
  not not_31 (not_31_out, n3_to_8_decoder_74138_3_p3);
  assign controlled_buffer_11_out = not_32_out ? not_14_out : 1'bz;  // Controlled_Buffer controlled_buffer_11
  not not_32 (not_32_out, L9);
  assign controlled_buffer_12_out = not_34_out ? not_30_out : 1'bz;  // Controlled_Buffer controlled_buffer_12
  assign controlled_buffer_13_out = not_33_out ? not_31_out : 1'bz;  // Controlled_Buffer controlled_buffer_13
  not not_33 (not_33_out, O3);
  not not_34 (not_34_out, O3);
  assign controlled_buffer_14_out = not_36_out ? not_15_out : 1'bz;  // Controlled_Buffer controlled_buffer_14
  assign controlled_buffer_15_out = not_35_out ? not_16_out : 1'bz;  // Controlled_Buffer controlled_buffer_15
  not not_35 (not_35_out, L9);
  not not_36 (not_36_out, L9);
  assign controlled_buffer_16_out = not_39_out ? not_28_out : 1'bz;  // Controlled_Buffer controlled_buffer_16
  assign controlled_buffer_17_out = not_38_out ? not_29_out : 1'bz;  // Controlled_Buffer controlled_buffer_17
  not not_37 (not_37_out, O3);
  not not_38 (not_38_out, O3);
  not not_39 (not_39_out, O3);
  or or_30 (S, 1'b0, controlled_inverter_1_out);
  assign controlled_buffer_18_out = not_40_out ? not_17_out : 1'bz;  // Controlled_Buffer controlled_buffer_18
  not not_40 (not_40_out, L9);
  assign controlled_buffer_19_out = not_42_out ? not_25_out : 1'bz;  // Controlled_Buffer controlled_buffer_19
  assign L5 = not_41_out ? not_26_out : 1'bz;  // Controlled_Buffer controlled_buffer_20
  assign controlled_buffer_21_out = not_37_out ? not_27_out : 1'bz;  // Controlled_Buffer controlled_buffer_21
  not not_41 (not_41_out, O3);
  not not_42 (not_42_out, O3);
  assign controlled_buffer_22_out = not_43_out ? not_18_out : 1'bz;  // Controlled_Buffer controlled_buffer_22
  assign controlled_buffer_23_out = not_44_out ? not_19_out : 1'bz;  // Controlled_Buffer controlled_buffer_23
  not not_43 (not_43_out, L9);
  not not_44 (not_44_out, L9);
  assign controlled_buffer_24_out = not_45_out ? controlled_buffer_13_out : 1'bz;  // Controlled_Buffer controlled_buffer_24
  not not_45 (not_45_out, and_66_out);
  or or_31 (or_31_out, controlled_buffer_11_out, controlled_buffer_6_out);
  or or_32 (or_32_out, controlled_buffer_14_out, controlled_buffer_7_out);
  or or_33 (or_33_out, controlled_buffer_8_out, controlled_buffer_15_out);
  or or_34 (or_34_out, controlled_buffer_18_out, controlled_buffer_9_out);
  or or_35 (or_35_out, L5, L4);
  or or_36 (or_36_out, L2, L1);
  or or_37 (or_37_out, controlled_buffer_24_out, or_31_out);
  and and_71 (L0, or_37_out, not_46_out);
  not not_46 (not_46_out, and_63_out);
  or or_38 (P, or_35_out, or_36_out);
  or or_39 (L1, controlled_buffer_12_out, or_32_out);
  or or_40 (L2, controlled_buffer_17_out, or_33_out);
  or or_41 (L3, controlled_buffer_16_out, or_34_out);
  or or_42 (L4, controlled_buffer_21_out, controlled_buffer_22_out);
  or or_43 (L6, controlled_buffer_19_out, controlled_buffer_23_out);

  assign L7 = 1'b0;
  assign L8 = 1'b0;
  assign Z = L0;

  // Notes on the sheet:
  //   A0B1
  //   A1A0
  //   AND
  //   equal
  //   or
  //   A1B1
  //   xor
  //   GREATER
  //   MULTIP 0
  //   MULTIP 1
  //   MULTIP2
  //   RESULT = 9
  //   SUM OUTPUT RIGHT
  //   A MODULO B
  //   A DIVISON B
  //   SIGN
  //   CARRY
  //   SUM OUTPUT LEFT
  //   SUB LEFT OUTPUT
  //   COMP OPCODE
  //   SUB RIGHT
  //   LESS
  //   MUX2
  //   L0
  //   L1
  //   MUX1
  //   A-B EKLE
  //   O2
  //   L2
  //   O1
  //   L3
  //   MULTIP OPCODE
  //   carry
  //   O0
  //   L0
  //   L1
  //   ÇARPMA / VEYA HARİÇ
  //   L2
  //   L3
  //   L4
  //   L6
  //   L3
  //   L0
  //   L1
  //   L2
endmodule

module Full_Adder (
  input  I_0,
  input  I_1,
  input  C_in,
  output S,
  output C_out
);

  wire and_1_out, and_2_out, xor_1_out;

  xor xor_1 (xor_1_out, I_0, I_1);
  xor xor_2 (S, xor_1_out, C_in);
  and and_1 (and_1_out, xor_1_out, C_in);
  and and_2 (and_2_out, I_0, I_1);
  or or_1 (C_out, and_1_out, and_2_out);
endmodule
